# Fritzing sketch WiFiSerialModem_R1V2 (saved by Fritzing 0.9.4)
circuit board: 10.1cm x 7.6cm
breadboards: 2

parts:
  NodeMCU_ESP8266_12E = ESP8266 NodeMCU LoLin module
  MR_LED = LED - 5mm [color="Red (633nm)" package="5 mm [THT]"]
  CD_LED = LED - 5mm [color="Red (633nm)" package="5 mm [THT]"]
  RXTX_LED = LED - 5mm [color="Red (633nm)" package="5 mm [THT]"]
  AA_LED = LED - 5mm [color="Red (633nm)" package="5 mm [THT]"]
  R1 = Resistor [tolerance=±5% resistance=1k package=THT]
  R2 = Resistor [tolerance=±5% resistance=1k package=THT]
  R3 = Resistor [tolerance=±5% resistance=1k package=THT]
  R4 = Resistor [tolerance=±5% resistance=1k package=THT]
  R6 = Resistor [tolerance=±5% resistance=10k package=THT]
  S1 = Round Pushbutton
  Serial_Module = female pin header, 4 pins [form="♀ (female)"]

nets:
  N1: NodeMCU_ESP8266_12E.D2, R1.Pin_1
  N2: NodeMCU_ESP8266_12E.D4, R6.Pin_1, S1.leg0
  N3: NodeMCU_ESP8266_12E.3V3, S1.leg1, Serial_Module.pin4
  N4: NodeMCU_ESP8266_12E.GND, MR_LED.cathode, CD_LED.cathode, RXTX_LED.cathode, AA_LED.cathode, R6.Pin_0, Serial_Module.pin1
  N5: NodeMCU_ESP8266_12E.D5, R3.Pin_1
  N6: NodeMCU_ESP8266_12E.D6, R2.Pin_1
  N7: NodeMCU_ESP8266_12E.D7, R4.Pin_1
  N8: NodeMCU_ESP8266_12E.RX, Serial_Module.pin2
  N9: NodeMCU_ESP8266_12E.TX, Serial_Module.pin3
  N10: MR_LED.anode, R1.Pin_0
  N11: CD_LED.anode, R2.Pin_0
  N12: RXTX_LED.anode, R3.Pin_0
  N13: AA_LED.anode, R4.Pin_0

notes:
  WiFi Serial
  Modem
  20210324-R1V2

custom parts:
  ESP8266 NodeMCU LoLin module: ESP8266 based NodeMCU
